# Fritzing sketch HandRemote-WiringDiagram (saved by Fritzing 0.9.3b)

parts:
  Part1 = Arduino Uno (Rev3)
  Part3 = Arduino Xbee Libellium Shield
  DFRobot_LCD_keypad_shield1 = LCD keypad Shield
  BuzzerDFR1 = BuzzerDFR0032
  R1 = Resistor [tolerance=±5% resistance=220k package=THT]
  R2 = Resistor [tolerance=±5% resistance=220 package=THT]

nets:
  N1: Part1.D8, DFRobot_LCD_keypad_shield1.D13
  N2: Part1.D9_PWM, DFRobot_LCD_keypad_shield1.TX
  N3: Part1.D10_PWM/SS, DFRobot_LCD_keypad_shield1.RX
  N4: Part1.D11_PWM/MOSI, Part3.2
  N5: Part1.D12/MISO, Part3.DOUT
  N6: Part1.D4, DFRobot_LCD_keypad_shield1.D2
  N7: Part1.D5_PWM, DFRobot_LCD_keypad_shield1.D3
  N8: Part1.D6_PWM, DFRobot_LCD_keypad_shield1.D11
  N9: Part1.D7, DFRobot_LCD_keypad_shield1.D12
  N10: Part3.M8RXD, DFRobot_LCD_keypad_shield1.VCC
  N11: Part3.M8TXD, DFRobot_LCD_keypad_shield1.GND#19
  N12: DFRobot_LCD_keypad_shield1.GND#4, R2.Pin_0
  N13: DFRobot_LCD_keypad_shield1.Vin, R1.Pin_0
  N14: DFRobot_LCD_keypad_shield1.A1, R1.Pin_1, R2.Pin_1
  N15: DFRobot_LCD_keypad_shield1.D0, BuzzerDFR1.Signal

notes:
  Active Buzzer
  D2 = Signal
  Voltage Divider for Battery Meter (A1)
  XBee DOUT>RX(D12)
  XBee DIN>TX(D11)
  Used Pins **
  D10 - LCD Backlight
  D9 - LCD Enable
  D8 - LCD RS
  D7 to D4 - LCD DB(0::4)
  Used Pin
  A0 - Keypad Buttons

custom parts:
  LCD keypad Shield: A 2 row LCD shield with buttons, and contrast regulator.
